// Logisim project memoryGame.circ as structural Verilog
module main (
  input  in_1
);

  wire and_2_out, and_3_out, COLUNA, CONFIRMA, L00, L01, L02, L03, L10, L11, L12, L13, L20, L21, L22, L23,
       L30, L31, L32, L33, LINHA, P1, P2, state0, state1, state2, state3;
  wire [1:0] COL, COL1, COL2, counter_3_q, LIN, LIN1, LIN2;
  wire [3:0] _00, _01, _02, _03, _10, _11, _12, _13, _20, _21, _22, _23, _30, _31, _32, _33, PONTOS_P1,
       PONTOS_P2;

  Button button_1 (.out(CONFIRMA));
  Button button_2 (.out(LINHA));
  Button button_3 (.out(COLUNA));
  LED led_1 (.in(P1));
  Hex_Digit_Display hex_digit_display_1 (.value(PONTOS_P1));  // open: dp
  LED led_2 (.in(P2));
  Hex_Digit_Display hex_digit_display_2 (.value(PONTOS_P2));  // open: dp
  Multiplexer #(.width(4), .enable("false")) multiplexer_1 (.in1(4'b0000), .out(_00), .sel(in_1));  // open: in0
  Multiplexer #(.width(4), .enable("false")) multiplexer_2 (.in1(4'b0000), .out(_00), .sel(in_1));  // open: in0
  Multiplexer #(.width(4), .enable("false")) multiplexer_3 (.in1(4'b0000), .out(_00), .sel(in_1));  // open: in0
  Multiplexer #(.width(4), .enable("false")) multiplexer_4 (.in1(4'b0000), .out(_00), .sel(in_1));  // open: in0
  LED led_3 (.in(L00));
  Hex_Digit_Display hex_digit_display_3 (.value(_00));  // open: dp
  LED led_4 (.in(L10));
  Hex_Digit_Display hex_digit_display_4 (.value(_10));  // open: dp
  LED led_5 (.in(L20));
  Hex_Digit_Display hex_digit_display_5 (.value(_20));  // open: dp
  LED led_6 (.in(L30));
  Hex_Digit_Display hex_digit_display_6 (.value(_30));  // open: dp
  Multiplexer #(.width(4), .enable("false")) multiplexer_5 (.in1(4'b0000), .out(_00), .sel(in_1));  // open: in0
  Multiplexer #(.width(4), .enable("false")) multiplexer_6 (.in1(4'b0000), .out(_00), .sel(in_1));  // open: in0
  Multiplexer #(.width(4), .enable("false")) multiplexer_7 (.in1(4'b0000), .out(_00), .sel(in_1));  // open: in0
  Multiplexer #(.width(4), .enable("false")) multiplexer_8 (.in1(4'b0000), .out(_00), .sel(in_1));  // open: in0
  Multiplexer #(.width(4), .enable("false")) multiplexer_9 (.in1(4'b0000), .out(_00), .sel(in_1));  // open: in0
  Multiplexer #(.width(4), .enable("false")) multiplexer_10 (.in1(4'b0000), .out(_00), .sel(in_1));  // open: in0
  Multiplexer #(.width(4), .enable("false")) multiplexer_11 (.in1(4'b0000), .out(_00), .sel(in_1));  // open: in0
  Multiplexer #(.width(4), .enable("false")) multiplexer_12 (.in1(4'b0000), .out(_00), .sel(in_1));  // open: in0
  LED led_7 (.in(L01));
  Hex_Digit_Display hex_digit_display_7 (.value(_01));  // open: dp
  LED led_8 (.in(L11));
  Hex_Digit_Display hex_digit_display_8 (.value(_11));  // open: dp
  LED led_9 (.in(L21));
  Hex_Digit_Display hex_digit_display_9 (.value(_21));  // open: dp
  LED led_10 (.in(L31));
  Hex_Digit_Display hex_digit_display_10 (.value(_31));  // open: dp
  // AND_Gate and_1 has open pins: in0=LIN1[0], in1=COL1[0], out=open
  LED led_11 (.in(L02));
  Hex_Digit_Display hex_digit_display_11 (.value(_02));  // open: dp
  LED led_12 (.in(L12));
  Hex_Digit_Display hex_digit_display_12 (.value(_12));  // open: dp
  LED led_13 (.in(L22));
  Hex_Digit_Display hex_digit_display_13 (.value(_22));  // open: dp
  LED led_14 (.in(L32));
  Hex_Digit_Display hex_digit_display_14 (.value(_32));  // open: dp
  Multiplexer #(.width(4), .enable("false")) multiplexer_13 (.in1(4'b0000), .out(_00), .sel(in_1));  // open: in0
  Multiplexer #(.width(4), .enable("false")) multiplexer_14 (.in1(4'b0000), .out(_00), .sel(in_1));  // open: in0
  Multiplexer #(.width(4), .enable("false")) multiplexer_15 (.in1(4'b0000), .out(_00), .sel(in_1));  // open: in0
  Multiplexer #(.width(4), .enable("false")) multiplexer_16 (.in1(4'b0000), .out(_00), .sel(in_1));  // open: in0
  // OR_Gate or_1 is placed but not wired
  LED led_15 (.in(L03));
  Hex_Digit_Display hex_digit_display_15 (.value(_03));  // open: dp
  LED led_16 (.in(L13));
  Hex_Digit_Display hex_digit_display_16 (.value(_13));  // open: dp
  LED led_17 (.in(L23));
  Hex_Digit_Display hex_digit_display_17 (.value(_23));  // open: dp
  LED led_18 (.in(L33));
  Hex_Digit_Display hex_digit_display_18 (.value(_33));  // open: dp
  and and_2 (and_2_out, CONFIRMA, state0);
  and and_3 (and_3_out, CONFIRMA, state1);
  Register #(.width(2)) register_1 (.D(COL), .Q(COL1), .clk(and_2_out));  // open: en, clr
  Register #(.width(2)) register_2 (.D(COL), .Q(COL2), .clk(and_3_out));  // open: en, clr
  Demultiplexer #(.select(4), .enable("false")) demultiplexer_1 (
    .out0(L00), .out1(L01), .out2(L02), .out3(L03), .out4(L10), .out5(L11), .out6(L12), .out7(L13),
    .out8(L20), .out9(L21), .out10(L22), .out11(L23), .out12(L30), .out13(L31), .out14(L32), .out15(L33),
    .in(1'b1), .sel({LIN, COL}));
  Register #(.width(2)) register_3 (.D(LIN), .Q(LIN1), .clk(and_2_out));  // open: en, clr
  Register #(.width(2)) register_4 (.D(LIN), .Q(LIN2), .clk(and_3_out));  // open: en, clr
  Counter #(.width(2), .max('h3)) counter_1 (.Q(COL), .clk(COLUNA));  // open: load, D, count, carry, clr
  Counter #(.width(2), .max('h3)) counter_2 (.Q(LIN), .clk(LINHA));  // open: load, D, count, carry, clr
  Counter #(.width(2), .max('h3)) counter_3 (
    .Q(counter_3_q), .clk(CONFIRMA), .clr(state3));  // open: load, D, count, carry
  and and_4 (state0, ~counter_3_q[0], ~counter_3_q[1]);  // AND_Gate
  and and_5 (state1, ~counter_3_q[1], counter_3_q[0]);  // AND_Gate
  and and_6 (state2, counter_3_q[1], ~counter_3_q[0]);  // AND_Gate
  and and_7 (state3, counter_3_q[1], counter_3_q[0]);
  // Pins of 1 and 2 bits meet at LIN1
  // Pins of 1 and 2 bits meet at COL1

  // Other names for the same wires on the sheet: v00 = in_1; xy[3:0] = {LIN, COL}

  // Notes on the sheet:
  //   JOGO DA MEMÓRIA
  //   Circuitos Digitais - Computação 2024.1
  //   Registrador das posições selecionadas
  //   Gerenciador de estados
endmodule
